# Fritzing sketch dynamic RE schematic (saved by Fritzing 0.9.4)
breadboards: 1

parts:
  S7 = Pushbutton [package="[THT]"]
  Mod1 = Raspberry Pi Pico
  Mod2 = Raspberry Pi Pico

nets:
  N1: S7.Pin_1, S7.Pin_2, Mod1.pin_3, Mod1.pin_8, Mod1.pin_13, Mod1.pin_18, Mod1.pin_23, Mod1.pin_28, Mod1.pin_33, Mod1.pin_38, Mod2.pin_3, Mod2.pin_8, Mod2.pin_13, Mod2.pin_18, Mod2.pin_23, Mod2.pin_28, Mod2.pin_33, Mod2.pin_38, Mod2.pin_42
  N2: S7.Pin_3, S7.Pin_4, Mod1.pin_30
  N3: Mod1.pin_4, Mod2.pin_41
  N4: Mod1.pin_5, Mod2.pin_43
  N5: Mod1.pin_6, Mod2.pin_2
  N6: Mod1.pin_7, Mod2.pin_1
  N7: Mod1.pin_39, Mod2.pin_39

custom parts:
  Raspberry Pi Pico: Raspberry Pi Pico. Based around the RP2040 microcontroller the Pico is a low cost microcontroller device bringing Raspberry Pi quality, cost, and easy of use to the microcontroller space. Jan 2021, fixed pcb so holes will be drilled for the pins. Added mounting holes to silkscreen (to drill mounting holes the user needs to drag a hole from core parts/pcb over the hole in silkscreen, by default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
