# Fritzing sketch oled and button schematic (saved by Fritzing 0.9.4)
breadboards: 1

parts:
  S7 = Pushbutton [package="[THT]"]
  Mod1 = Raspberry Pi Pico
  OLED1 = OLED 128x64 I2C Monochrome Display
  S8 = Pushbutton [package="[THT]"]
  S9 = Pushbutton [package="[THT]"]
  S10 = Pushbutton [package="[THT]"]
  S11 = Pushbutton [package="[THT]"]
  S12 = Pushbutton [package="[THT]"]

nets:
  N1: S7.Pin_1, S7.Pin_2, Mod1.pin_3, Mod1.pin_8, Mod1.pin_13, Mod1.pin_18, Mod1.pin_23, Mod1.pin_28, Mod1.pin_33, Mod1.pin_38, OLED1.GND, S8.Pin_3, S8.Pin_4, S9.Pin_3, S9.Pin_4, S10.Pin_3, S10.Pin_4, S11.Pin_3, S11.Pin_4, S12.Pin_3, S12.Pin_4
  N2: S7.Pin_3, S7.Pin_4, Mod1.pin_30
  N3: Mod1.pin_6, OLED1.SDA
  N4: Mod1.pin_7, OLED1.SCK
  N5: Mod1.pin_12, S8.Pin_1, S8.Pin_2
  N6: Mod1.pin_14, S9.Pin_1, S9.Pin_2
  N7: Mod1.pin_15, S10.Pin_1, S10.Pin_2
  N8: Mod1.pin_16, S11.Pin_1, S11.Pin_2
  N9: Mod1.pin_17, S12.Pin_1, S12.Pin_2
  N10: Mod1.pin_36, OLED1.VDD

custom parts:
  Raspberry Pi Pico: Raspberry Pi Pico. Based around the RP2040 microcontroller the Pico is a low cost microcontroller device bringing Raspberry Pi quality, cost, and easy of use to the microcontroller space. Jan 2021, fixed pcb so holes will be drilled for the pins. Added mounting holes to silkscreen (to drill mounting holes the user needs to drag a hole from core parts/pcb over the hole in silkscreen, by default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
